# Fritzing sketch ChickenDoor (saved by Fritzing 0.9.3b)

parts:
  M1 = DC Motor
  VCC1 = Battery
  Raspberry_Pi_1 = Raspberry Pi 3 [part_number=RPI-3-V1.2]
  S1 = H-Bridge with L298N

nets:
  N1: M1.pin_1, S1.M1-02, S1.M2-01
  N2: M1.pin_2, S1.M1-01
  GND: VCC1.-, Raspberry_Pi_1.GND, S1.GND
  N3: VCC1.+, S1.12V
  N4: Raspberry_Pi_1.GPIO17, S1.IN1
  N5: Raspberry_Pi_1.GPIO27, S1.IN2

custom parts:
  H-Bridge with L298N: h-bridge
